// Logisim project wagner.circ as structural Verilog: 5 circuits, main circuit main
module main (
  input  in_1,
  input  in_2,
  input  in_3,
  output out_4,
  output out_5
);

  D d_1 (.A(in_2), .B(in_1), .VEM_1(in_3), .VAL_1(out_4), .S(out_5));
endmodule

module D (
  input  A,
  input  B,
  input  VEM_1,
  output S,
  output VAL_1
);

  wire and_1_out, and_2_out, and_3_out, xor_1_out;

  xor xor_1 (xor_1_out, A, B);
  and and_1 (and_1_out, A, VEM_1);
  and and_2 (and_2_out, A, B);
  and and_3 (and_3_out, B, VEM_1);
  xor xor_2 (S, xor_1_out, VEM_1);
  or or_1 (VAL_1, and_1_out, and_2_out, and_3_out);
endmodule

module aDD4 (
);

  D d_1 ();  // open: A, B, VEM_1, VAL_1, S
  D d_2 ();  // open: A, B, VEM_1, VAL_1, S
  D d_3 ();  // open: A, B, VEM_1, VAL_1, S
  D d_4 ();  // open: A, B, VEM_1, VAL_1, S
endmodule

module exec1 (
  input  A,
  input  B,
  input  C,
  output out_4
);

  wire and_1_out, or_1_out, xor_1_out;

  xor xor_1 (xor_1_out, A, B);
  or or_1 (or_1_out, xor_1_out, B);
  and and_1 (and_1_out, A, or_1_out);
  or or_2 (out_4, and_1_out, C);
endmodule

module EXECMAIN (
  input  A,
  input  B,
  input  C,
  output out_4
);

  wire and_1_out, or_1_out, xor_1_out;

  xor xor_1 (xor_1_out, A, B);
  or or_1 (or_1_out, xor_1_out, B);
  and and_1 (and_1_out, A, or_1_out);
  or or_2 (out_4, and_1_out, C);
endmodule
